// Logisim project SP1_COMPUTER.circ as structural Verilog
module DecoderInstruct (
  input  in_1,
  input  in_2,
  input  in_3,
  input  in_4,
  output out_5,
  output out_6,
  output out_7,
  output out_8,
  output out_9
);

  wire not_1_out, not_2_out, not_3_out, not_4_out;

  not not_1 (not_1_out, in_2);
  not not_2 (not_2_out, in_1);
  not not_3 (not_3_out, in_3);
  not not_4 (not_4_out, in_4);
  and and_1 (out_5, not_4_out, not_3_out, not_1_out, not_2_out);
  and and_2 (out_6, in_4, not_3_out, not_1_out, not_2_out);
  and and_3 (out_7, not_4_out, in_3, not_1_out, not_2_out);
  and and_4 (out_8, in_4, in_3, not_1_out, not_2_out);
  nand nand_1 (out_9, in_4, in_3, in_2, in_1);

  // Notes on the sheet:
  //   LDA
  //   ADD
  //   SUB
  //   OUT
  //   \HLT
endmodule

module DringCounter (
  input  CLK,
  input  nCLR,
  output T1,
  output T2,
  output T3,
  output T4,
  output T5,
  output T6
);

  wire not_1_out, not_2_out, not_3_out, not_4_out, not_5_out, not_6_out, not_7_out, not_8_out, not_9_out,
       not_10_out, not_11_out, not_12_out;

  not not_1 (not_1_out, CLK);
  not not_2 (not_2_out, nCLR);
  D_Flip_Flop d_ff_1 (.clk(not_1_out), .D(T6), .Q(T1), .preset(not_2_out));  // open: Qn, en, reset
  D_Flip_Flop d_ff_2 (.clk(not_3_out), .D(T1), .Q(T2), .reset(not_4_out));  // open: Qn, preset, en
  not not_3 (not_3_out, CLK);
  not not_4 (not_4_out, nCLR);
  D_Flip_Flop d_ff_3 (.clk(not_5_out), .D(T2), .Q(T3), .reset(not_6_out));  // open: Qn, preset, en
  not not_5 (not_5_out, CLK);
  not not_6 (not_6_out, nCLR);
  not not_7 (not_7_out, CLK);
  not not_8 (not_8_out, CLK);
  D_Flip_Flop d_ff_4 (.clk(not_7_out), .D(T3), .Q(T4), .reset(not_9_out));  // open: Qn, preset, en
  not not_9 (not_9_out, nCLR);
  D_Flip_Flop d_ff_5 (.clk(not_8_out), .D(T4), .Q(T5), .reset(not_10_out));  // open: Qn, preset, en
  not not_10 (not_10_out, nCLR);
  D_Flip_Flop d_ff_6 (.clk(not_11_out), .D(T5), .Q(T6), .reset(not_12_out));  // open: Qn, preset, en
  not not_11 (not_11_out, CLK);
  not not_12 (not_12_out, nCLR);
endmodule

module ControlMatrix (
  input  in_1,
  input  in_2,
  input  in_3,
  input  in_4,
  input  in_5,
  input  in_6,
  output out_7,
  output Cp,
  output Ep
);

  wire decoderinstruct_1_out_5, decoderinstruct_1_out_6, decoderinstruct_1_out_7, decoderinstruct_1_out_8,
       dringcounter_1_t3, dringcounter_1_t4, dringcounter_1_t5, dringcounter_1_t6;

  DecoderInstruct decoderinstruct_1 (
    .out_5(decoderinstruct_1_out_5), .out_6(decoderinstruct_1_out_6), .out_7(decoderinstruct_1_out_7),
    .out_8(decoderinstruct_1_out_8), .out_9(out_7), .in_1(in_3), .in_2(in_4), .in_3(in_5), .in_4(in_6));
  DringCounter dringcounter_1 (
    .CLK(in_1), .nCLR(in_2), .T1(Ep), .T2(Cp), .T3(dringcounter_1_t3), .T4(dringcounter_1_t4),
    .T5(dringcounter_1_t5), .T6(dringcounter_1_t6));
  C39 c39_1 ();  // open: in_1, in_2, in_3, in_4, in_5, in_6, in_7, in_8, out_9, out_10, out_11, out_12
  C39 c39_2 ();  // open: in_1, in_2, in_3, in_4, in_5, in_6, in_7, in_8, out_9, out_10, out_11, out_12
  C39 c39_3 ();  // open: in_1, in_2, in_3, in_4, in_5, in_6, in_7, in_8, out_9, out_10, out_11, out_12
  C39 c39_4 ();  // open: in_1, in_2, in_3, in_4, in_5, in_6, in_7, in_8, out_9, out_10, out_11, out_12
  C43 c43_1 ();  // open: in_1, in_2, in_3, in_4, in_5, in_6, out_7, out_8, out_9

  // Notes on the sheet:
  //   C39
  //   C40
  //   C41
  //   C42
endmodule

module C39 (
  input  in_1,
  input  in_2,
  input  in_3,
  input  in_4,
  input  in_5,
  input  in_6,
  input  in_7,
  input  in_8,
  output out_9,
  output out_10,
  output out_11,
  output out_12
);

  nand nand_1 (out_9, in_1, in_2);
  nand nand_2 (out_10, in_3, in_4);
  nand nand_3 (out_11, in_5, in_6);
  nand nand_4 (out_12, in_7, in_8);
endmodule

module C43 (
  input  in_1,
  input  in_2,
  input  in_3,
  input  in_4,
  input  in_5,
  input  in_6,
  output out_7,
  output out_8,
  output out_9
);

  nand nand_1 (out_8, in_3, in_4);
  nand nand_2 (out_7, in_1, in_2);
  nand nand_3 (out_9, in_5, in_6);
endmodule

module SAP_ARC (
);

  ProgramCounter programcounter_1 ();  // open: Cp, nCLK, nCLR, Ep, _4, _3, _2, _1
endmodule

module ProgramCounter (
  input  Cp,
  input  nCLK,
  input  nCLR,
  input  Ep,
  output _4,
  output _3,
  output _2,
  output _1
);

  wire j_k_ff_1_q, j_k_ff_2_q, j_k_ff_3_q, j_k_ff_4_q, not_1_out, not_2_out, not_3_out, not_4_out, not_5_out,
       not_6_out, not_7_out, not_8_out;

  J_K_Flip_Flop j_k_ff_1 (.J(Cp), .clk(not_1_out), .K(Cp), .Q(j_k_ff_1_q), .reset(not_2_out));  // open: Qn, preset, en
  not not_1 (not_1_out, nCLK);
  not not_2 (not_2_out, nCLR);
  not not_3 (not_3_out, j_k_ff_1_q);
  assign _1 = Ep ? j_k_ff_1_q : 1'bz;  // Controlled_Buffer controlled_buffer_1
  not not_4 (not_4_out, j_k_ff_2_q);
  J_K_Flip_Flop j_k_ff_2 (.J(Cp), .clk(not_3_out), .K(Cp), .Q(j_k_ff_2_q), .reset(not_5_out));  // open: Qn, preset, en
  not not_5 (not_5_out, nCLR);
  assign _2 = Ep ? j_k_ff_2_q : 1'bz;  // Controlled_Buffer controlled_buffer_2
  J_K_Flip_Flop j_k_ff_3 (.J(Cp), .clk(not_4_out), .K(Cp), .Q(j_k_ff_3_q), .reset(not_6_out));  // open: Qn, preset, en
  not not_6 (not_6_out, nCLR);
  assign _3 = Ep ? j_k_ff_3_q : 1'bz;  // Controlled_Buffer controlled_buffer_3
  not not_7 (not_7_out, j_k_ff_3_q);
  not not_8 (not_8_out, nCLR);
  J_K_Flip_Flop j_k_ff_4 (.J(Cp), .clk(not_7_out), .K(Cp), .Q(j_k_ff_4_q), .reset(not_8_out));  // open: Qn, preset, en
  assign _4 = Ep ? j_k_ff_4_q : 1'bz;  // Controlled_Buffer controlled_buffer_4
endmodule
